# Fritzing sketch 7seg (saved by Fritzing 0.3.8b)
breadboards: 2

parts:
  Arduino1 = Arduino
  Q1 = NPN-Transistor [package="TO92 [THT]"]
  R1 = 220 Ω Resistor [package=THT]
  Q1_2 = NPN-Transistor [package="TO92 [THT]"]
  R1_2 = 220 Ω Resistor [package=THT]
  Q1_3 = NPN-Transistor [package="TO92 [THT]"]
  R1_3 = 220 Ω Resistor [package=THT]
  Q1_4 = NPN-Transistor [package="TO92 [THT]"]
  R1_4 = 220 Ω Resistor [package=THT]
  J1 = Screw terminal [package=THT]
  J1_2 = Screw terminal [package=THT]
  J1_3 = Screw terminal [package=THT]
  J1_4 = Screw terminal [package=THT]
  J1_5 = Screw terminal [package=THT]
  J1_6 = Screw terminal [package=THT]
  J1_7 = Screw terminal [package=THT]
  Q1_5 = NPN-Transistor [package="TO92 [THT]"]
  R1_5 = 220 Ω Resistor [package=THT]
  Q1_6 = NPN-Transistor [package="TO92 [THT]"]
  R1_6 = 220 Ω Resistor [package=THT]
  Q1_7 = NPN-Transistor [package="TO92 [THT]"]
  R1_7 = 220 Ω Resistor [package=THT]
  Q1_8 = NPN-Transistor [package="TO92 [THT]"]
  R1_8 = 220 Ω Resistor [package=THT]
  Q1_9 = NPN-Transistor [package="TO92 [THT]"]
  R1_9 = 220 Ω Resistor [package=THT]
  Q1_10 = NPN-Transistor [package="TO92 [THT]"]
  R1_10 = 220 Ω Resistor [package=THT]
  Q1_11 = NPN-Transistor [package="TO92 [THT]"]
  Q1_12 = NPN-Transistor [package="TO92 [THT]"]
  R1_11 = 220 Ω Resistor [package=THT]
  R1_12 = 220 Ω Resistor [package=THT]

nets:
  N1: Arduino1.D13, R1_11.Pin_0
  N2: Arduino1.D12, R1_12.Pin_0
  N3: Arduino1.D11, R1_10.Pin_0
  N4: Arduino1.D10, R1_9.Pin_0
  N5: Arduino1.D9, R1_8.Pin_0
  N6: Arduino1.D8, R1_7.Pin_0
  N7: Arduino1.D7, R1_6.Pin_0
  N8: Arduino1.D6, R1_5.Pin_0
  N9: Arduino1.D5, R1_4.Pin_0
  N10: Arduino1.D4, R1_3.Pin_0
  N11: Arduino1.D3, R1_2.Pin_0
  N12: Arduino1.D2, R1.Pin_0
  N13: Arduino1.+5V, Q1_9.emitter, Q1_10.emitter, Q1_11.emitter, Q1_12.emitter
  N14: Arduino1.GND, Q1.collector, Q1_2.collector, Q1_3.collector, Q1_4.collector, Q1_5.collector, Q1_6.collector, Q1_7.collector, Q1_8.collector
  N15: Q1.emitter, J1_7.pin2
  N16: Q1.base, R1.Pin_1
  N17: Q1_2.emitter, J1_7.pin1
  N18: Q1_2.base, R1_2.Pin_1
  N19: Q1_3.emitter, J1_6.pin2
  N20: Q1_3.base, R1_3.Pin_1
  N21: Q1_4.emitter, J1_6.pin1
  N22: Q1_4.base, R1_4.Pin_1
  N23: J1.pin1, Q1_11.collector
  N24: J1.pin2, Q1_12.collector
  N25: J1_2.pin2, Q1_10.collector
  N26: J1_3.pin1, Q1_9.collector
  N27: J1_4.pin1, Q1_8.emitter
  N28: J1_4.pin2, Q1_7.emitter
  N29: J1_5.pin1, Q1_6.emitter
  N30: J1_5.pin2, Q1_5.emitter
  N31: Q1_5.base, R1_5.Pin_1
  N32: Q1_6.base, R1_6.Pin_1
  N33: Q1_7.base, R1_7.Pin_1
  N34: Q1_8.base, R1_8.Pin_1
  N35: Q1_9.base, R1_9.Pin_1
  N36: Q1_10.base, R1_10.Pin_1
  N37: Q1_11.base, R1_11.Pin_1
  N38: Q1_12.base, R1_12.Pin_1
